// Logisim project inc.circ as structural Verilog: 2 circuits, main circuit main
module main (
  input  RST,
  input  DIN,
  output DOUT_VLD,
  output [7:0] DOUT
);

  wire and_1_out, and_2_out, and_3_out, clock_1_out, clock_2_out, clock_3_out, clock_4_out, clock_5_out,
       clock_6_out, clock_7_out, clock_8_out, clock_9_out, clock_10_out, clock_11_out, counter_1_carry,
       counter_2_carry, demultiplexer_1_out0, demultiplexer_1_out1, demultiplexer_1_out2,
       demultiplexer_1_out3, demultiplexer_1_out4, demultiplexer_1_out5, demultiplexer_1_out6,
       demultiplexer_1_out7, fsm_1_rx_clr, fsm_1_rx_end, fsm_1_rx_offset, fsm_1_rx_read, or_1_out, or_2_out,
       or_3_out;
  wire [2:0] counter_2_q;
  wire [3:0] counter_1_q;

  Clock clock_1 (.out(clock_1_out));
  Counter #(.max('hf), .width(4)) counter_1 (
    .clr(RST), .load(1'b0), .up(1'b1), .count(and_2_out), .clk(clock_2_out), .carry(counter_1_carry),
    .Q(counter_1_q));  // open: D
  Clock clock_2 (.out(clock_2_out));
  FSM fsm_1 (
    .CLK(clock_1_out), .RST(RST), .DIN(DIN), .CNT3(counter_2_q), .CNT4(counter_1_q),
    .RX_OFFSET(fsm_1_rx_offset), .RX_READ(fsm_1_rx_read), .RX_END(fsm_1_rx_end), .RX_VLD(DOUT_VLD),
    .RX_CLR(fsm_1_rx_clr));
  or or_1 (or_1_out, RST, fsm_1_rx_clr);
  or or_2 (or_2_out, fsm_1_rx_read, fsm_1_rx_end, counter_2_carry);
  and and_1 (and_1_out, fsm_1_rx_read, counter_1_carry);
  Counter #(.max('h7), .width(3)) counter_2 (
    .clr(RST), .load(1'b0), .up(1'b1), .count(or_3_out), .clk(clock_3_out), .carry(counter_2_carry),
    .Q(counter_2_q));  // open: D
  or or_3 (or_3_out, fsm_1_rx_offset, and_1_out);
  Clock clock_3 (.out(clock_3_out));
  and and_2 (and_2_out, or_2_out, ~fsm_1_rx_clr);  // AND_Gate
  and and_3 (and_3_out, and_1_out, DIN);
  Demultiplexer #(.select(3)) demultiplexer_1 (
    .out0(demultiplexer_1_out0), .out1(demultiplexer_1_out1), .out2(demultiplexer_1_out2),
    .out3(demultiplexer_1_out3), .out4(demultiplexer_1_out4), .out5(demultiplexer_1_out5),
    .out6(demultiplexer_1_out6), .out7(demultiplexer_1_out7), .in(and_3_out), .sel(counter_2_q));
  J_K_Flip_Flop j_k_ff_1 (
    .J(demultiplexer_1_out0), .K(1'b0), .clk(clock_4_out), .Q(DOUT[0]), .reset(or_1_out));  // open: Qn, preset
  Clock clock_4 (.out(clock_4_out));
  J_K_Flip_Flop j_k_ff_2 (
    .J(demultiplexer_1_out1), .K(1'b0), .clk(clock_5_out), .Q(DOUT[1]), .reset(or_1_out));  // open: Qn, preset
  Clock clock_5 (.out(clock_5_out));
  J_K_Flip_Flop j_k_ff_3 (
    .J(demultiplexer_1_out2), .K(1'b0), .clk(clock_6_out), .Q(DOUT[2]), .reset(or_1_out));  // open: Qn, preset
  Clock clock_6 (.out(clock_6_out));
  J_K_Flip_Flop j_k_ff_4 (
    .J(demultiplexer_1_out3), .K(1'b0), .clk(clock_7_out), .Q(DOUT[3]), .reset(or_1_out));  // open: Qn, preset
  Clock clock_7 (.out(clock_7_out));
  J_K_Flip_Flop j_k_ff_5 (
    .J(demultiplexer_1_out4), .K(1'b0), .clk(clock_8_out), .Q(DOUT[4]), .reset(or_1_out));  // open: Qn, preset
  Clock clock_8 (.out(clock_8_out));
  J_K_Flip_Flop j_k_ff_6 (
    .J(demultiplexer_1_out5), .K(1'b0), .clk(clock_9_out), .Q(DOUT[5]), .reset(or_1_out));  // open: Qn, preset
  Clock clock_9 (.out(clock_9_out));
  J_K_Flip_Flop j_k_ff_7 (
    .J(demultiplexer_1_out6), .K(1'b0), .clk(clock_10_out), .Q(DOUT[6]), .reset(or_1_out));  // open: Qn, preset
  Clock clock_10 (.out(clock_10_out));
  J_K_Flip_Flop j_k_ff_8 (
    .J(demultiplexer_1_out7), .K(1'b0), .clk(clock_11_out), .Q(DOUT[7]), .reset(or_1_out));  // open: Qn, preset
  Clock clock_11 (.out(clock_11_out));
endmodule

module FSM (
  input  CLK,
  input  RST,
  input  DIN,
  input  [2:0] CNT3,
  input  [3:0] CNT4,
  output RX_OFFSET,
  output RX_READ,
  output RX_END,
  output RX_VLD,
  output RX_CLR
);

  wire and_1_out, and_2_out, and_3_out, and_4_out, and_5_out, and_6_out, and_7_out, or_1_out,
       shift_register_1_p2, shift_register_1_p7, shift_register_1_p8;

  and and_1 (and_1_out, CNT3[0], CNT3[1], CNT3[2]);
  and and_2 (and_2_out, CNT4[0], CNT4[1], CNT4[2], CNT4[3]);
  and and_3 (and_3_out, ~DIN, shift_register_1_p7);  // AND_Gate
  and and_4 (and_4_out, and_1_out, shift_register_1_p8);
  and and_5 (and_5_out, and_1_out, and_2_out, RX_READ);
  and and_6 (and_6_out, and_2_out, RX_END);
  and and_7 (and_7_out, and_1_out, RX_CLR);
  or or_1 (or_1_out, CLK, RST);
  // Shift_Register #(.length(6)) shift_register_1: pin names not known; wires that end beside it: RST, shift_register_1_p2, or_1_out, RX_CLR, 1'b1, 1'b0, shift_register_1_p7, shift_register_1_p8, RX_READ, RX_END, RX_VLD
  or or_2 (shift_register_1_p2, and_3_out, and_4_out, and_5_out, RST, and_6_out, and_7_out, RX_VLD);
  or or_3 (RX_OFFSET, shift_register_1_p8, RX_VLD, RX_CLR);
endmodule
