// Logisim project inc.circ as structural Verilog: 2 circuits, main circuit main
module main (
  input  DIN,
  output DOUT_VLD,
  output [7:0] DOUT
);

  wire and_1_out, and_2_out, and_3_out, and_4_out, and_5_out, and_6_out, clock_1_out, clock_2_out,
       clock_3_out, clock_4_out, clock_5_out, clock_6_out, clock_7_out, clock_8_out, clock_9_out,
       clock_10_out, clock_11_out, clock_12_out, demultiplexer_1_out0, demultiplexer_1_out1,
       demultiplexer_1_out2, demultiplexer_1_out3, demultiplexer_1_out4, demultiplexer_1_out5,
       demultiplexer_1_out6, demultiplexer_1_out7, fsm_1_read, fsm_1_wait_first, fsm_1_wait_offset,
       fsm_1_wait_start, j_k_ff_1_q, j_k_ff_2_q, or_1_out, or_2_out;
  wire [2:0] counter_2_q;
  wire [3:0] counter_1_q;

  Counter #(.max('hf), .width(4)) counter_1 (
    .clr(and_1_out), .up(1'b1), .count(or_1_out), .clk(clock_1_out), .Q(counter_1_q));  // open: load, D, carry
  Clock clock_1 (.out(clock_1_out));
  FSM fsm_1 (
    .DIN(DIN), .WAIT_DONE(or_2_out), .READ_DONE(and_6_out), .WAIT_START(fsm_1_wait_start),
    .WAIT_OFFSET(fsm_1_wait_offset), .WAIT_FIRST(fsm_1_wait_first), .READ(fsm_1_read), .DATA_VALID(DOUT_VLD));  // open: WAIT_END
  or or_1 (or_1_out, fsm_1_wait_offset, fsm_1_wait_first, fsm_1_read);
  and and_1 (and_1_out, fsm_1_wait_offset, and_2_out);
  and and_2 (and_2_out, counter_1_q[0], counter_1_q[1], counter_1_q[2]);
  and and_3 (and_3_out, counter_1_q[0], counter_1_q[1], counter_1_q[2], counter_1_q[3]);
  or or_2 (or_2_out, and_3_out, and_1_out);
  Clock clock_2 (.out(clock_2_out));
  and and_4 (and_4_out, DIN, and_3_out);
  Counter #(.max('h7), .width(3)) counter_2 (
    .up(1'b1), .count(and_5_out), .clk(clock_3_out), .Q(counter_2_q));  // open: clr, load, D, carry
  and and_5 (and_5_out, fsm_1_read, and_3_out, j_k_ff_2_q);
  Clock clock_3 (.out(clock_3_out));
  J_K_Flip_Flop #(.trigger("falling")) j_k_ff_1 (
    .J(and_3_out), .K(1'b0), .clk(clock_2_out), .Q(j_k_ff_1_q), .reset(and_6_out));  // open: Qn, preset
  J_K_Flip_Flop #(.trigger("falling")) j_k_ff_2 (
    .J(j_k_ff_1_q), .K(1'b0), .clk(clock_4_out), .Q(j_k_ff_2_q), .reset(and_6_out));  // open: Qn, preset
  Clock clock_4 (.out(clock_4_out));
  Demultiplexer #(.select(3)) demultiplexer_1 (
    .out0(demultiplexer_1_out0), .out1(demultiplexer_1_out1), .out2(demultiplexer_1_out2),
    .out3(demultiplexer_1_out3), .out4(demultiplexer_1_out4), .out5(demultiplexer_1_out5),
    .out6(demultiplexer_1_out6), .out7(demultiplexer_1_out7), .in(and_4_out), .sel(counter_2_q));
  and and_6 (and_6_out, counter_2_q[0], counter_2_q[1], counter_2_q[2]);
  J_K_Flip_Flop j_k_ff_3 (
    .J(demultiplexer_1_out0), .K(fsm_1_wait_start), .clk(clock_5_out), .Q(DOUT[0]));  // open: Qn, preset, reset
  Clock clock_5 (.out(clock_5_out));
  J_K_Flip_Flop j_k_ff_4 (
    .J(demultiplexer_1_out1), .K(fsm_1_wait_start), .clk(clock_6_out), .Q(DOUT[1]));  // open: Qn, preset, reset
  Clock clock_6 (.out(clock_6_out));
  J_K_Flip_Flop j_k_ff_5 (
    .J(demultiplexer_1_out2), .K(fsm_1_wait_start), .clk(clock_7_out), .Q(DOUT[2]));  // open: Qn, preset, reset
  Clock clock_7 (.out(clock_7_out));
  J_K_Flip_Flop j_k_ff_6 (
    .J(demultiplexer_1_out3), .K(fsm_1_wait_start), .clk(clock_8_out), .Q(DOUT[3]));  // open: Qn, preset, reset
  Clock clock_8 (.out(clock_8_out));
  J_K_Flip_Flop j_k_ff_7 (
    .J(demultiplexer_1_out4), .K(fsm_1_wait_start), .clk(clock_9_out), .Q(DOUT[4]));  // open: Qn, preset, reset
  Clock clock_9 (.out(clock_9_out));
  J_K_Flip_Flop j_k_ff_8 (
    .J(demultiplexer_1_out5), .K(fsm_1_wait_start), .clk(clock_10_out), .Q(DOUT[5]));  // open: Qn, preset, reset
  Clock clock_10 (.out(clock_10_out));
  J_K_Flip_Flop j_k_ff_9 (
    .J(demultiplexer_1_out6), .K(fsm_1_wait_start), .clk(clock_11_out), .Q(DOUT[6]));  // open: Qn, preset, reset
  Clock clock_11 (.out(clock_11_out));
  J_K_Flip_Flop j_k_ff_10 (
    .J(demultiplexer_1_out7), .K(fsm_1_wait_start), .clk(clock_12_out), .Q(DOUT[7]));  // open: Qn, preset, reset
  Clock clock_12 (.out(clock_12_out));
endmodule

module FSM (
  input  DIN,
  input  WAIT_DONE,
  input  READ_DONE,
  output WAIT_START,
  output WAIT_OFFSET,
  output WAIT_FIRST,
  output READ,
  output WAIT_END,
  output DATA_VALID
);

  wire and_1_out, and_2_out, and_3_out, and_4_out, and_5_out, clock_1_out, nor_1_out, or_1_out,
       shift_register_1_p1, shift_register_1_p2;

  and and_1 (and_1_out, ~DIN, WAIT_START);  // AND_Gate
  and and_2 (and_2_out, WAIT_DONE, WAIT_OFFSET);
  and and_3 (and_3_out, WAIT_DONE, WAIT_FIRST);
  and and_4 (and_4_out, READ_DONE, READ);
  and and_5 (and_5_out, DIN, WAIT_END);
  // Shift_Register #(.length(6)) shift_register_1: pin names not known; wires that end beside it: shift_register_1_p1, shift_register_1_p2, WAIT_START, WAIT_OFFSET, WAIT_FIRST, READ, WAIT_END
  Clock clock_1 (.out(clock_1_out));
  and and_6 (shift_register_1_p1, clock_1_out, or_1_out);
  or or_1 (or_1_out, and_1_out, and_2_out, and_3_out, and_4_out, and_5_out, shift_register_1_p2);
  or or_2 (shift_register_1_p2, nor_1_out, DATA_VALID);
  nor nor_1 (nor_1_out, WAIT_START, WAIT_OFFSET, WAIT_FIRST, READ, WAIT_END, DATA_VALID);
endmodule
